# Fritzing sketch pendeteksi suhu pada aquarium (saved by Fritzing 0.9.3b)
circuit board: 8.46667cm x 5.64444cm
breadboards: 1

parts:
  LCD_16X2 = LCD screen
  DS18B20 = DS18B20 1-Wire Temperature Sensor Probe
  i2_C = LCM1602 IIC [part_number="LCM1602 IIC" chip_label="LCM1602 IIC" package="DIP (Dual Inline) [THT]"]
  ESP32_D1_R32 = >Wemos D1 R32
  R_4_7_Ohm = Resistor [tolerance=±5% resistance=220 package="2512 [SMD]"]

nets:
  VSS: LCD_16X2.VSS, i2_C.VSS
  VDD: LCD_16X2.VDD, i2_C.VDD
  N1: LCD_16X2.V0, i2_C.V0
  N2: LCD_16X2.RS, i2_C.RS
  N3: LCD_16X2.R/W, i2_C.RW
  N4: LCD_16X2.E, i2_C.E
  N5: LCD_16X2.DB0, i2_C.D0
  N6: LCD_16X2.DB1, i2_C.D1
  N7: LCD_16X2.DB2, i2_C.D2
  N8: LCD_16X2.DB3, i2_C.D3
  N9: LCD_16X2.DB4, i2_C.D4
  N10: LCD_16X2.DB5, i2_C.D5
  N11: LCD_16X2.DB6, i2_C.D6
  N12: LCD_16X2.DB7, i2_C.D7
  N13: LCD_16X2.LED+, i2_C.A
  N14: LCD_16X2.LED-, i2_C.K
  GND: DS18B20.GND, i2_C.GND, ESP32_D1_R32.GND
  N15: DS18B20.DQ, ESP32_D1_R32.IO2, R_4_7_Ohm.Pin_0
  VDD_2: DS18B20.VDD, ESP32_D1_R32.3V3, R_4_7_Ohm.Pin_1
  VCC: i2_C.VCC, ESP32_D1_R32.5V
  N16: i2_C.SDA, ESP32_D1_R32.SDA
  N17: i2_C.SCL, ESP32_D1_R32.SCL
  N18: i2_C.LED_A, i2_C.LED_B

custom parts:
  LCM1602 IIC: I2C-Module to use a 1602 or 2004 LCD on with the wire.h libory Serial LCD Modul
  >Wemos D1 R32: Wemos D1 R32 - This board is used with dual-mode Wi-Fi and Bluetooth chips, which is safe, reliable, and scalable to a variety of applications. DC in 5V-12V, 1 analog input(3.2V max input), a Micro USB connection, Compatible with D1 R32=WiFi+bluetooth+UNO

// code stored in the sketch: AnalogReadSerial2LCD_LED.ino
#include <OneWire.h>
#include <DallasTemperature.h>
#include <LiquidCrystal_I2C.h>

// Pins untuk Sensor DS18B20
#define ONE_WIRE_BUS 4

// Pins untuk LCD 16x2
#define LCD_ADDR 0x27
#define LCD_ROWS 2
#define LCD_COLS 16

OneWire oneWire(ONE_WIRE_BUS);
DallasTemperature sensors(&oneWire);

LiquidCrystal_I2C lcd(LCD_ADDR, LCD_COLS, LCD_ROWS);

void setup() {
  Serial.begin(9600);
  sensors.begin();
  lcd.begin(LCD_COLS, LCD_ROWS);
}

void loop() {
  sensors.requestTemperatures();
  float waterTempC = sensors.getTempCByIndex(0);

  if (waterTempC != DEVICE_DISCONNECTED_C) {
    lcd.clear();
    lcd.setCursor(0, 0);
    lcd.print("Suhu Air:");
    lcd.setCursor(0, 1);
    lcd.print(waterTempC);
    lcd.print(" C");

    Serial.print("Suhu Air: ");
    Serial.print(waterTempC);
    Serial.println(" C");
  } else {
    lcd.clear();
    lcd.setCursor(0, 0);
    lcd.print("Sensor tidak");
    lcd.setCursor(0, 1);
    lcd.print("terdeteksi");
    
    Serial.println("Sensor tidak terdeteksi");
  }

  delay(1000); // Delay satu detik antara pembacaan suhu
}
